// Logisim project memory_game.circ as structural Verilog
module main (
  output out_1,
  output out_2
);

  wire b0, b1, b2, b3, b4, b5, b6, b7, b8, b9, Play, Reset;
  wire [4:0] single_display_1_out_2, single_display_1_out_3, single_display_1_out_4, single_display_1_out_5,
       single_display_1_out_6, single_display_2_out_2, single_display_2_out_3, single_display_2_out_4,
       single_display_2_out_5, single_display_2_out_6, single_display_3_out_2, single_display_3_out_3,
       single_display_3_out_4, single_display_3_out_5, single_display_3_out_6, single_display_4_out_2,
       single_display_4_out_3, single_display_4_out_4, single_display_4_out_5, single_display_4_out_6,
       single_display_5_out_2, single_display_5_out_3, single_display_5_out_4, single_display_5_out_5,
       single_display_5_out_6, single_display_mirrored_1_out_2, single_display_mirrored_1_out_3,
       single_display_mirrored_1_out_4, single_display_mirrored_1_out_5, single_display_mirrored_1_out_6,
       single_display_mirrored_2_out_2, single_display_mirrored_2_out_3, single_display_mirrored_2_out_4,
       single_display_mirrored_2_out_5, single_display_mirrored_2_out_6, single_display_mirrored_3_out_2,
       single_display_mirrored_3_out_3, single_display_mirrored_3_out_4, single_display_mirrored_3_out_5,
       single_display_mirrored_3_out_6, single_display_mirrored_4_out_2, single_display_mirrored_4_out_3,
       single_display_mirrored_4_out_4, single_display_mirrored_4_out_5, single_display_mirrored_4_out_6,
       single_display_mirrored_5_out_2, single_display_mirrored_5_out_3, single_display_mirrored_5_out_4,
       single_display_mirrored_5_out_5, single_display_mirrored_5_out_6;
  wire [8:0] d0, d1, d2, d3, d4, d5, d6, d7, d8, d9;

  Button button_1 (.out(Reset));
  Button button_2 (.out(Play));
  Hex_Digit_Display hex_digit_display_1 ();  // open: value, dp
  Hex_Digit_Display hex_digit_display_2 ();  // open: value, dp
  single_display single_display_1 (
    .in_1(d0), .out_2(single_display_1_out_2), .out_3(single_display_1_out_3),
    .out_4(single_display_1_out_4), .out_5(single_display_1_out_5), .out_6(single_display_1_out_6));
  DotMatrix #(.matrixrows(5)) dotmatrix_1 (
    .col0(single_display_1_out_6), .col1(single_display_1_out_5), .col2(single_display_1_out_4),
    .col3(single_display_1_out_3), .col4(single_display_1_out_2));
  DotMatrix #(.matrixrows(5)) dotmatrix_2 (
    .col0(single_display_2_out_6), .col1(single_display_2_out_5), .col2(single_display_2_out_4),
    .col3(single_display_2_out_3), .col4(single_display_2_out_2));
  DotMatrix #(.matrixrows(5)) dotmatrix_3 (
    .col0(single_display_mirrored_1_out_2), .col1(single_display_mirrored_1_out_3),
    .col2(single_display_mirrored_1_out_4), .col3(single_display_mirrored_1_out_5),
    .col4(single_display_mirrored_1_out_6));
  DotMatrix #(.matrixrows(5)) dotmatrix_4 (
    .col0(single_display_mirrored_2_out_2), .col1(single_display_mirrored_2_out_3),
    .col2(single_display_mirrored_2_out_4), .col3(single_display_mirrored_2_out_5),
    .col4(single_display_mirrored_2_out_6));
  single_display_mirrored single_display_mirrored_1 (
    .in_1(d1), .out_2(single_display_mirrored_1_out_2), .out_3(single_display_mirrored_1_out_3),
    .out_4(single_display_mirrored_1_out_4), .out_5(single_display_mirrored_1_out_5),
    .out_6(single_display_mirrored_1_out_6));
  single_display_mirrored single_display_mirrored_2 (
    .in_1(d3), .out_2(single_display_mirrored_2_out_2), .out_3(single_display_mirrored_2_out_3),
    .out_4(single_display_mirrored_2_out_4), .out_5(single_display_mirrored_2_out_5),
    .out_6(single_display_mirrored_2_out_6));
  Button button_3 (.out(b0));
  Button button_4 (.out(b1));
  single_display single_display_2 (
    .in_1(d2), .out_2(single_display_2_out_2), .out_3(single_display_2_out_3),
    .out_4(single_display_2_out_4), .out_5(single_display_2_out_5), .out_6(single_display_2_out_6));
  DotMatrix #(.matrixrows(5)) dotmatrix_5 (
    .col0(single_display_3_out_6), .col1(single_display_3_out_5), .col2(single_display_3_out_4),
    .col3(single_display_3_out_3), .col4(single_display_3_out_2));
  DotMatrix #(.matrixrows(5)) dotmatrix_6 (
    .col0(single_display_mirrored_3_out_2), .col1(single_display_mirrored_3_out_3),
    .col2(single_display_mirrored_3_out_4), .col3(single_display_mirrored_3_out_5),
    .col4(single_display_mirrored_3_out_6));
  single_display_mirrored single_display_mirrored_3 (
    .in_1(d5), .out_2(single_display_mirrored_3_out_2), .out_3(single_display_mirrored_3_out_3),
    .out_4(single_display_mirrored_3_out_4), .out_5(single_display_mirrored_3_out_5),
    .out_6(single_display_mirrored_3_out_6));
  Button button_5 (.out(b2));
  Button button_6 (.out(b4));
  Button button_7 (.out(b3));
  Button button_8 (.out(b5));
  Hex_Digit_Display hex_digit_display_3 ();  // open: value, dp
  single_display single_display_3 (
    .in_1(d4), .out_2(single_display_3_out_2), .out_3(single_display_3_out_3),
    .out_4(single_display_3_out_4), .out_5(single_display_3_out_5), .out_6(single_display_3_out_6));
  single_display single_display_4 (
    .in_1(d6), .out_2(single_display_4_out_2), .out_3(single_display_4_out_3),
    .out_4(single_display_4_out_4), .out_5(single_display_4_out_5), .out_6(single_display_4_out_6));
  DotMatrix #(.matrixrows(5)) dotmatrix_7 (
    .col0(single_display_4_out_6), .col1(single_display_4_out_5), .col2(single_display_4_out_4),
    .col3(single_display_4_out_3), .col4(single_display_4_out_2));
  DotMatrix #(.matrixrows(5)) dotmatrix_8 (
    .col0(single_display_mirrored_4_out_2), .col1(single_display_mirrored_4_out_3),
    .col2(single_display_mirrored_4_out_4), .col3(single_display_mirrored_4_out_5),
    .col4(single_display_mirrored_4_out_6));
  single_display_mirrored single_display_mirrored_4 (
    .in_1(d7), .out_2(single_display_mirrored_4_out_2), .out_3(single_display_mirrored_4_out_3),
    .out_4(single_display_mirrored_4_out_4), .out_5(single_display_mirrored_4_out_5),
    .out_6(single_display_mirrored_4_out_6));
  Button button_9 (.out(b6));
  Button button_10 (.out(b8));
  Button button_11 (.out(b7));
  Button button_12 (.out(b9));
  Hex_Digit_Display hex_digit_display_4 ();  // open: value, dp
  single_display single_display_5 (
    .in_1(d8), .out_2(single_display_5_out_2), .out_3(single_display_5_out_3),
    .out_4(single_display_5_out_4), .out_5(single_display_5_out_5), .out_6(single_display_5_out_6));
  DotMatrix #(.matrixrows(5)) dotmatrix_9 (
    .col0(single_display_5_out_6), .col1(single_display_5_out_5), .col2(single_display_5_out_4),
    .col3(single_display_5_out_3), .col4(single_display_5_out_2));
  DotMatrix #(.matrixrows(5)) dotmatrix_10 (
    .col0(single_display_mirrored_5_out_2), .col1(single_display_mirrored_5_out_3),
    .col2(single_display_mirrored_5_out_4), .col3(single_display_mirrored_5_out_5),
    .col4(single_display_mirrored_5_out_6));
  single_display_mirrored single_display_mirrored_5 (
    .in_1(d9), .out_2(single_display_mirrored_5_out_2), .out_3(single_display_mirrored_5_out_3),
    .out_4(single_display_mirrored_5_out_4), .out_5(single_display_mirrored_5_out_5),
    .out_6(single_display_mirrored_5_out_6));
  set_cards set_cards_1 (
    .in_1(Play), .in_2(Reset), .out_3(d0), .out_4(d1), .out_5(d2), .out_6(d3), .out_7(d4), .out_8(d5),
    .out_9(d6), .out_10(d7), .out_11(d8), .out_12(d9));
  buttons buttons_1 (
    .in_1(b0), .in_2(b1), .in_3(b2), .in_4(b3), .in_5(b4), .in_6(b5), .in_7(b6), .in_8(b7), .in_9(b8),
    .in_10(b9), .out_13(out_1), .out_14(out_2));  // open: in_11, in_12
endmodule

module set_cards (
  input  in_1,
  input  in_2,
  output [8:0] out_3,
  output [8:0] out_4,
  output [8:0] out_5,
  output [8:0] out_6,
  output [8:0] out_7,
  output [8:0] out_8,
  output [8:0] out_9,
  output [8:0] out_10,
  output [8:0] out_11,
  output [8:0] out_12
);

  wire clk, doCount, end_b, eq0, eq1, eq2, eq3, eq4, eq5, eq6, eq7, eq8, eq9, n0, n1, n2, n3, n4, n5, n6, n7,
       n8, n9, not_1_out, or_1_out, r0, r1, r2, r3, r4, r5, r6, r7, r8, r9, start;
  wire [3:0] count, randN;
  wire [8:0] c0, c1, c2, c3, c4, d0, d1, d2, d3, d4, d5, d6, d7, d8, d9, multiplexer_1_out;

  Clock clock_1 (.out(clk));
  deck deck_1 (.in_1(in_1), .in_2(in_2), .out_3(c0), .out_4(c1), .out_5(c2), .out_6(c3), .out_7(c4), .out_8(end_b));
  Register #(.width(9)) register_1 (.D(d0), .en(r0), .clk(clk), .Q(out_3), .clr(in_2));
  Register #(.width(9)) register_2 (.D(d2), .en(r2), .clk(clk), .Q(out_5), .clr(in_2));
  Register #(.width(9)) register_3 (.D(d4), .en(r4), .clk(clk), .Q(out_7), .clr(in_2));
  Register #(.width(9)) register_4 (.D(d6), .en(r6), .clk(clk), .Q(out_9), .clr(in_2));
  Register #(.width(9)) register_5 (.D(d8), .en(r8), .clk(clk), .Q(out_11), .clr(in_2));
  Multiplexer #(.select(4), .width(9)) multiplexer_1 (
    .in0(c0), .in1(c0), .in2(c1), .in3(c1), .in4(c2), .in5(c2), .in6(c3), .in7(c3), .in8(c4), .in9(c4),
    .out(multiplexer_1_out), .sel(count));  // open: in10, in11, in12, in13, in14, in15
  Random #(.width(4)) random_1 (.next(start), .clk(clk), .out(randN));  // open: clr
  Demultiplexer #(.select(4), .width(9)) demultiplexer_1 (
    .out0(d0), .out1(d1), .out2(d2), .out3(d3), .out4(d4), .out5(d5), .out6(d6), .out7(d7), .out8(d8),
    .out9(d9), .in(multiplexer_1_out), .sel(randN));  // open: out10, out11, out12, out13, out14, out15
  Register #(.width(9)) register_6 (.D(d1), .en(r1), .clk(clk), .Q(out_4), .clr(in_2));
  Register #(.width(9)) register_7 (.D(d3), .en(r3), .clk(clk), .Q(out_6), .clr(in_2));
  Register #(.width(9)) register_8 (.D(d5), .en(r5), .clk(clk), .Q(out_8), .clr(in_2));
  Register #(.width(9)) register_9 (.D(d7), .en(r7), .clk(clk), .Q(out_10), .clr(in_2));
  Register #(.width(9)) register_10 (.D(d9), .en(r9), .clk(clk), .Q(out_12), .clr(in_2));
  Counter #(.max('ha), .width(4)) counter_1 (
    .clr(not_1_out), .count(doCount), .clk(clk), .Q(count));  // open: load, up, D, carry
  not not_1 (not_1_out, end_b);
  Comparator #(.width(9)) comparator_1 (.a(out_3), .b({9{1'b0}}), .eq(eq0));  // open: gt, lt
  Comparator #(.width(9)) comparator_2 (.a(out_5), .b({9{1'b0}}), .eq(eq2));  // open: gt, lt
  Comparator #(.width(9)) comparator_3 (.a(out_7), .b({9{1'b0}}), .eq(eq4));  // open: gt, lt
  Comparator #(.width(9)) comparator_4 (.a(out_9), .b({9{1'b0}}), .eq(eq6));  // open: gt, lt
  Comparator #(.width(9)) comparator_5 (.a(out_11), .b({9{1'b0}}), .eq(eq8));  // open: gt, lt
  and and_1 (r0, n0, eq0);
  and and_2 (r2, n2, eq2);
  and and_3 (r4, n4, eq4);
  and and_4 (r6, n6, eq6);
  and and_5 (r8, n8, eq8);
  Comparator #(.width(9)) comparator_6 (.a(out_4), .b({9{1'b0}}), .eq(eq1));  // open: gt, lt
  Comparator #(.width(9)) comparator_7 (.a(out_6), .b({9{1'b0}}), .eq(eq3));  // open: gt, lt
  Comparator #(.width(9)) comparator_8 (.a(out_8), .b({9{1'b0}}), .eq(eq5));  // open: gt, lt
  Comparator #(.width(9)) comparator_9 (.a(out_10), .b({9{1'b0}}), .eq(eq7));  // open: gt, lt
  Comparator #(.width(9)) comparator_10 (.a(out_12), .b({9{1'b0}}), .eq(eq9));  // open: gt, lt
  and and_6 (r1, n1, eq1);
  and and_7 (r3, n3, eq3);
  and and_8 (r5, n5, eq5);
  and and_9 (r7, n7, eq7);
  and and_10 (r9, n9, eq9);
  Multiplexer #(.select(4)) multiplexer_2 (
    .in0(r0), .in1(r1), .in2(r2), .in3(r3), .in4(r4), .in5(r5), .in6(r6), .in7(r7), .in8(r8), .in9(r9),
    .in10(1'b0), .in11(1'b0), .in12(1'b0), .in13(1'b0), .in14(1'b0), .in15(1'b0), .out(doCount), .sel(randN));
  or or_1 (or_1_out, eq0, eq1, eq2, eq3, eq4, eq5, eq6, eq7, eq8, eq9);
  Demultiplexer #(.select(4)) demultiplexer_2 (
    .out0(n0), .out1(n1), .out2(n2), .out3(n3), .out4(n4), .out5(n5), .out6(n6), .out7(n7), .out8(n8),
    .out9(n9), .in(start), .sel(randN));  // open: out10, out11, out12, out13, out14, out15
  and and_11 (start, or_1_out, end_b);

  // Other names for the same wires on the sheet: q0[8:0] = out_3; q1[8:0] = out_4; q2[8:0] = out_5; q3[8:0] = out_6;
  //   q4[8:0] = out_7; q5[8:0] = out_8; q6[8:0] = out_9; q7[8:0] = out_10; q8[8:0] = out_11; q9[8:0] = out_12;
  //   reset = in_2; set = in_1
endmodule

module deck (
  input  in_1,
  input  in_2,
  output [8:0] out_3,
  output [8:0] out_4,
  output [8:0] out_5,
  output [8:0] out_6,
  output [8:0] out_7,
  output out_8
);

  wire clk, not_1_out, r0, r1, r2, r3, r4, start;
  wire [2:0] count;
  wire [8:0] c0, c1, c2, c3, c4, random_1_out;

  Clock clock_1 (.out(clk));
  Register #(.width(9)) register_1 (.D(c0), .en(r0), .clk(clk), .Q(out_3), .clr(in_2));
  Register #(.width(9)) register_2 (.D(c1), .en(r1), .clk(clk), .Q(out_6), .clr(in_2));
  and and_1 (start, in_1, ~out_8);  // AND_Gate
  Random #(.width(9)) random_1 (.next(not_1_out), .clk(clk), .out(random_1_out));  // open: clr
  not not_1 (not_1_out, out_8);
  Register #(.width(9)) register_3 (.D(c2), .en(r2), .clk(clk), .Q(out_4), .clr(in_2));
  Register #(.width(9)) register_4 (.D(c3), .en(r3), .clk(clk), .Q(out_7), .clr(in_2));
  Demultiplexer #(.select(3), .width(9)) demultiplexer_1 (
    .out0(c0), .out1(c1), .out2(c2), .out3(c3), .out4(c4), .in(random_1_out), .sel(count));  // open: out5, out6, out7
  Register #(.width(9)) register_5 (.D(c4), .en(r4), .clk(clk), .Q(out_5), .clr(in_2));
  Counter #(.max('h5), .width(3)) counter_1 (
    .clr(in_2), .count(start), .clk(clk), .carry(out_8), .Q(count));  // open: load, up, D
  Decoder #(.select(3)) decoder_1 (
    .out0(r0), .out1(r1), .out2(r2), .out3(r3), .out4(r4), .sel(count));  // open: out5, out6, out7, en

  // Other names for the same wires on the sheet: reset = in_2; set = in_1; stop = out_8
endmodule

module buttons (
  input  in_1,
  input  in_2,
  input  in_3,
  input  in_4,
  input  in_5,
  input  in_6,
  input  in_7,
  input  in_8,
  input  in_9,
  input  in_10,
  input  in_11,
  input  in_12,
  output out_13,
  output out_14
);

  wire bx, c0, c1, clk, reset, stop, undriven, undriven_2;
  wire [3:0] b_sel;
  wire [8:0] d0, d1, d2, d3, d4, d5, d6, d7, d8, d9, dx, register_1_q, register_2_q;

  Clock clock_1 (.out(clk));
  set_cards set_cards_1 (
    .in_1(in_1), .in_2(in_2), .out_3(d0), .out_4(d1), .out_5(d2), .out_6(d3), .out_7(d4), .out_8(d5),
    .out_9(d6), .out_10(d7), .out_11(d8), .out_12(d9));
  Priority_Encoder #(.select(4)) priority_encoder_1 (
    .in0(in_3), .in1(in_4), .in2(in_5), .in3(in_6), .in4(in_7), .in5(in_8), .in6(in_9), .in7(in_10),
    .in8(in_11), .in9(in_12), .out(b_sel));  // open: in10, in11, in12, in13, in14, in15, gs, en_out, en_in
  Multiplexer #(.select(4), .width(9)) multiplexer_1 (
    .in0(d0), .in1(d1), .in2(d2), .in3(d3), .in4(d4), .in5(d5), .in6(d6), .in7(d7), .in8(d8), .in9(d9),
    .out(dx), .sel(b_sel));  // open: in10, in11, in12, in13, in14, in15
  ExactlyOne xor_1 (
    .out(bx), .in0(in_3), .in1(in_4), .in2(in_5), .in3(in_6), .in4(in_7), .in5(in_8), .in6(in_9),
    .in7(in_10), .in8(in_11), .in9(in_12));
  Register #(.width(9)) register_1 (.D(dx), .en(c0), .clk(bx), .Q(register_1_q), .clr(reset));
  Register #(.width(9)) register_2 (.D(dx), .en(c1), .clk(bx), .Q(register_2_q), .clr(reset));
  Counter #(.max('h2), .width(2)) counter_1 (
    .clr(undriven_2), .count(undriven), .clk(bx), .carry(stop), .Q({c1, c0}));  // open: load, up, D
  Comparator #(.width(9)) comparator_1 (.a(register_1_q), .b(register_2_q), .eq(out_13));  // open: gt, lt
  not not_1 (out_14, out_13);

  // Other names for the same wires on the sheet: b0 = in_3; b1 = in_4; b2 = in_5; b3 = in_6; b4 = in_7; b5 = in_8;
  //   b6 = in_9; b7 = in_10; b8 = in_11; b9 = in_12
endmodule

// _
module single_display (
  input  [8:0] in_1,
  output [4:0] out_2,
  output [4:0] out_3,
  output [4:0] out_4,
  output [4:0] out_5,
  output [4:0] out_6
);

  wire [4:0] bit_extender_1_out, bit_extender_2_out, bit_extender_3_out;

  assign bit_extender_1_out = {{2{1'b0}}, in_1[2:0]};  // Bit_Extender bit_extender_1
  assign bit_extender_2_out = {{2{1'b0}}, in_1[5:3]};  // Bit_Extender bit_extender_2
  assign bit_extender_3_out = {{2{1'b0}}, in_1[8:6]};  // Bit_Extender bit_extender_3
  Shifter #(.width(5)) shifter_1 (.in(bit_extender_1_out), .\dist (3'b001), .out(out_3));
  Shifter #(.width(5)) shifter_2 (.in(bit_extender_2_out), .\dist (3'b001), .out(out_4));
  Shifter #(.width(5)) shifter_3 (.in(bit_extender_3_out), .\dist (3'b001), .out(out_5));

  assign out_2 = {5{1'b0}};
  assign out_6 = {5{1'b0}};
endmodule

// __
module single_display_mirrored (
  input  [8:0] in_1,
  output [4:0] out_2,
  output [4:0] out_3,
  output [4:0] out_4,
  output [4:0] out_5,
  output [4:0] out_6
);

  wire [4:0] bit_extender_1_out, bit_extender_2_out, bit_extender_3_out;

  assign bit_extender_1_out = {{2{1'b0}}, in_1[2:0]};  // Bit_Extender bit_extender_1
  assign bit_extender_2_out = {{2{1'b0}}, in_1[5:3]};  // Bit_Extender bit_extender_2
  assign bit_extender_3_out = {{2{1'b0}}, in_1[8:6]};  // Bit_Extender bit_extender_3
  Shifter #(.width(5)) shifter_1 (.in(bit_extender_1_out), .\dist (3'b001), .out(out_5));
  Shifter #(.width(5)) shifter_2 (.in(bit_extender_2_out), .\dist (3'b001), .out(out_4));
  Shifter #(.width(5)) shifter_3 (.in(bit_extender_3_out), .\dist (3'b001), .out(out_3));

  assign out_2 = {5{1'b0}};
  assign out_6 = {5{1'b0}};
endmodule
